// Logisim project RiscV32_Logisim_harvard-3-(2).circ as structural Verilog: 20 circuits, main circuit main
module main (
);

  wire button_1_out, clock_1_out, cpu_1_illegal, cpu_1_load, cpu_1_store, or_1_out;
  wire [2:0] cpu_1_memwidth;
  wire [31:0] cpu_1_memaddr, cpu_1_pc, cpu_1_storevalue, memory_1_loadvalue, rom_1_data;

  Clock clock_1 (.out(clock_1_out));
  Button button_1 (.out(button_1_out));
  or or_1 (or_1_out, cpu_1_illegal, clock_1_out);
  CPU cpu_1 (
    .Instruction(rom_1_data), .LoadValue(memory_1_loadvalue), .Clock(or_1_out), .Reset(button_1_out),
    .Illegal(cpu_1_illegal), .MemWidth(cpu_1_memwidth), .Store(cpu_1_store), .Load(cpu_1_load),
    .MemAddr(cpu_1_memaddr), .StoreValue(cpu_1_storevalue), .PC(cpu_1_pc));
  ROM #(.addrWidth(24), .dataWidth(32)) rom_1 (.addr(cpu_1_pc[25:2]), .data(rom_1_data));
  Memory memory_1 (
    .Width(cpu_1_memwidth), .Store(cpu_1_store), .Load(cpu_1_load), .Address(cpu_1_memaddr),
    .StoreValue(cpu_1_storevalue), .Clock(or_1_out), .LoadValue(memory_1_loadvalue));

  // Notes on the sheet:
  //   contents of rom_1 (hex, n*v repeats v):
  //   93 113 193 213 293 3e800093 7d008113 c1810193 83018213 3e820293 1000317 fd830313
endmodule

module Extractor (
  input  [31:0] Instruction,
  input  [2:0] Format,
  output [6:0] Opcode,
  output [4:0] RD,
  output [2:0] Funct3,
  output [4:0] RS1,
  output [4:0] RS2,
  output [6:0] funct7,
  output [31:0] Immediate
);

  Multiplexer #(.select(3), .width(32)) multiplexer_1 (
    .in1({{21{Instruction[31]}}, Instruction[30:20]}),
    .in2({{21{Instruction[31]}}, Instruction[30:25], Instruction[11:7]}),
    .in3({{20{Instruction[31]}}, Instruction[7], Instruction[30:25], Instruction[11:8], 1'b0}),
    .in4({Instruction[31:12], {12{1'b0}}}),
    .in5({{12{Instruction[31]}}, Instruction[19:12], Instruction[20], Instruction[30:21], 1'b0}),
    .in6({32{1'b0}}), .in7({32{1'b0}}), .out(Immediate), .sel(Format));  // open: in0

  assign Funct3 = Instruction[14:12];
  assign funct7 = Instruction[31:25];
  assign Opcode = Instruction[6:0];
  assign RD = Instruction[11:7];
  assign RS1 = Instruction[19:15];
  assign RS2 = Instruction[24:20];

  // Notes on the sheet:
  //   I-type
  //   S-type
  //   B-type
  //   U-type
  //   J-type
endmodule

module Registers16 (
  input  Write,
  input  [3:0] RD,
  input  Clock,
  input  [31:0] Data,
  input  [3:0] RS1,
  input  [3:0] RS2,
  output [31:0] Out1,
  output [31:0] Out2
);

  wire decoder_1_out0, decoder_1_out1, decoder_1_out2, decoder_1_out3, decoder_1_out4, decoder_1_out5,
       decoder_1_out6, decoder_1_out7, decoder_1_out8, decoder_1_out9, decoder_1_out10, decoder_1_out11,
       decoder_1_out12, decoder_1_out13, decoder_1_out14, decoder_1_out15;
  wire [31:0] register_1_q, register_2_q, register_3_q, register_4_q, register_5_q, register_6_q,
       register_7_q, register_8_q, register_9_q, register_10_q, register_11_q, register_12_q, register_13_q,
       register_14_q, register_15_q, register_16_q;

  Multiplexer #(.select(4), .width(32)) multiplexer_1 (
    .in0(register_1_q), .in1(register_2_q), .in2(register_3_q), .in3(register_4_q), .in4(register_5_q),
    .in5(register_6_q), .in6(register_7_q), .in7(register_8_q), .in8(register_9_q), .in9(register_10_q),
    .in10(register_11_q), .in11(register_12_q), .in12(register_13_q), .in13(register_14_q),
    .in14(register_15_q), .in15(register_16_q), .out(Out1), .sel(RS1));
  Multiplexer #(.select(4), .width(32)) multiplexer_2 (
    .in0(register_1_q), .in1(register_2_q), .in2(register_3_q), .in3(register_4_q), .in4(register_5_q),
    .in5(register_6_q), .in6(register_7_q), .in7(register_8_q), .in8(register_9_q), .in9(register_10_q),
    .in10(register_11_q), .in11(register_12_q), .in12(register_13_q), .in13(register_14_q),
    .in14(register_15_q), .in15(register_16_q), .out(Out2), .sel(RS2));
  Decoder #(.select(4)) decoder_1 (
    .out0(decoder_1_out0), .out1(decoder_1_out1), .out2(decoder_1_out2), .out3(decoder_1_out3),
    .out4(decoder_1_out4), .out5(decoder_1_out5), .out6(decoder_1_out6), .out7(decoder_1_out7),
    .out8(decoder_1_out8), .out9(decoder_1_out9), .out10(decoder_1_out10), .out11(decoder_1_out11),
    .out12(decoder_1_out12), .out13(decoder_1_out13), .out14(decoder_1_out14), .out15(decoder_1_out15),
    .sel(RD), .en(Write));
  Register #(.trigger("falling"), .width(32)) register_1 (
    .D(Data), .en(decoder_1_out0), .clk(Clock), .Q(register_1_q));  // open: clr
  Register #(.trigger("falling"), .width(32)) register_2 (
    .D(Data), .en(decoder_1_out1), .clk(Clock), .Q(register_2_q));  // open: clr
  Register #(.trigger("falling"), .width(32)) register_3 (
    .D(Data), .en(decoder_1_out2), .clk(Clock), .Q(register_3_q));  // open: clr
  Register #(.trigger("falling"), .width(32)) register_4 (
    .D(Data), .en(decoder_1_out3), .clk(Clock), .Q(register_4_q));  // open: clr
  Register #(.trigger("falling"), .width(32)) register_5 (
    .D(Data), .en(decoder_1_out4), .clk(Clock), .Q(register_5_q));  // open: clr
  Register #(.trigger("falling"), .width(32)) register_6 (
    .D(Data), .en(decoder_1_out5), .clk(Clock), .Q(register_6_q));  // open: clr
  Register #(.trigger("falling"), .width(32)) register_7 (
    .D(Data), .en(decoder_1_out6), .clk(Clock), .Q(register_7_q));  // open: clr
  Register #(.trigger("falling"), .width(32)) register_8 (
    .D(Data), .en(decoder_1_out7), .clk(Clock), .Q(register_8_q));  // open: clr
  Register #(.trigger("falling"), .width(32)) register_9 (
    .D(Data), .en(decoder_1_out8), .clk(Clock), .Q(register_9_q));  // open: clr
  Register #(.trigger("falling"), .width(32)) register_10 (
    .D(Data), .en(decoder_1_out9), .clk(Clock), .Q(register_10_q));  // open: clr
  Register #(.trigger("falling"), .width(32)) register_11 (
    .D(Data), .en(decoder_1_out10), .clk(Clock), .Q(register_11_q));  // open: clr
  Register #(.trigger("falling"), .width(32)) register_12 (
    .D(Data), .en(decoder_1_out11), .clk(Clock), .Q(register_12_q));  // open: clr
  Register #(.trigger("falling"), .width(32)) register_13 (
    .D(Data), .en(decoder_1_out12), .clk(Clock), .Q(register_13_q));  // open: clr
  Register #(.trigger("falling"), .width(32)) register_14 (
    .D(Data), .en(decoder_1_out13), .clk(Clock), .Q(register_14_q));  // open: clr
  Register #(.trigger("falling"), .width(32)) register_15 (
    .D(Data), .en(decoder_1_out14), .clk(Clock), .Q(register_15_q));  // open: clr
  Register #(.trigger("falling"), .width(32)) register_16 (
    .D(Data), .en(decoder_1_out15), .clk(Clock), .Q(register_16_q));  // open: clr
endmodule

module Registers16WithZero (
  input  Write,
  input  [3:0] RD,
  input  Clock,
  input  [31:0] Data,
  input  [3:0] RS1,
  input  [3:0] RS2,
  output [31:0] Out1,
  output [31:0] Out2
);

  wire decoder_1_out1, decoder_1_out2, decoder_1_out3, decoder_1_out4, decoder_1_out5, decoder_1_out6,
       decoder_1_out7, decoder_1_out8, decoder_1_out9, decoder_1_out10, decoder_1_out11, decoder_1_out12,
       decoder_1_out13, decoder_1_out14, decoder_1_out15;
  wire [31:0] register_1_q, register_2_q, register_3_q, register_4_q, register_5_q, register_6_q,
       register_7_q, register_8_q, register_9_q, register_10_q, register_11_q, register_12_q, register_13_q,
       register_14_q, register_15_q;

  Multiplexer #(.select(4), .width(32)) multiplexer_1 (
    .in0({32{1'b0}}), .in1(register_1_q), .in2(register_2_q), .in3(register_3_q), .in4(register_4_q),
    .in5(register_5_q), .in6(register_6_q), .in7(register_7_q), .in8(register_8_q), .in9(register_9_q),
    .in10(register_10_q), .in11(register_11_q), .in12(register_12_q), .in13(register_13_q),
    .in14(register_14_q), .in15(register_15_q), .out(Out1), .sel(RS1));
  Multiplexer #(.select(4), .width(32)) multiplexer_2 (
    .in0({32{1'b0}}), .in1(register_1_q), .in2(register_2_q), .in3(register_3_q), .in4(register_4_q),
    .in5(register_5_q), .in6(register_6_q), .in7(register_7_q), .in8(register_8_q), .in9(register_9_q),
    .in10(register_10_q), .in11(register_11_q), .in12(register_12_q), .in13(register_13_q),
    .in14(register_14_q), .in15(register_15_q), .out(Out2), .sel(RS2));
  Decoder #(.select(4)) decoder_1 (
    .out1(decoder_1_out1), .out2(decoder_1_out2), .out3(decoder_1_out3), .out4(decoder_1_out4),
    .out5(decoder_1_out5), .out6(decoder_1_out6), .out7(decoder_1_out7), .out8(decoder_1_out8),
    .out9(decoder_1_out9), .out10(decoder_1_out10), .out11(decoder_1_out11), .out12(decoder_1_out12),
    .out13(decoder_1_out13), .out14(decoder_1_out14), .out15(decoder_1_out15), .sel(RD), .en(Write));  // open: out0
  Register #(.trigger("falling"), .width(32)) register_1 (
    .D(Data), .en(decoder_1_out1), .clk(Clock), .Q(register_1_q));  // open: clr
  Register #(.trigger("falling"), .width(32)) register_2 (
    .D(Data), .en(decoder_1_out2), .clk(Clock), .Q(register_2_q));  // open: clr
  Register #(.trigger("falling"), .width(32)) register_3 (
    .D(Data), .en(decoder_1_out3), .clk(Clock), .Q(register_3_q));  // open: clr
  Register #(.trigger("falling"), .width(32)) register_4 (
    .D(Data), .en(decoder_1_out4), .clk(Clock), .Q(register_4_q));  // open: clr
  Register #(.trigger("falling"), .width(32)) register_5 (
    .D(Data), .en(decoder_1_out5), .clk(Clock), .Q(register_5_q));  // open: clr
  Register #(.trigger("falling"), .width(32)) register_6 (
    .D(Data), .en(decoder_1_out6), .clk(Clock), .Q(register_6_q));  // open: clr
  Register #(.trigger("falling"), .width(32)) register_7 (
    .D(Data), .en(decoder_1_out7), .clk(Clock), .Q(register_7_q));  // open: clr
  Register #(.trigger("falling"), .width(32)) register_8 (
    .D(Data), .en(decoder_1_out8), .clk(Clock), .Q(register_8_q));  // open: clr
  Register #(.trigger("falling"), .width(32)) register_9 (
    .D(Data), .en(decoder_1_out9), .clk(Clock), .Q(register_9_q));  // open: clr
  Register #(.trigger("falling"), .width(32)) register_10 (
    .D(Data), .en(decoder_1_out10), .clk(Clock), .Q(register_10_q));  // open: clr
  Register #(.trigger("falling"), .width(32)) register_11 (
    .D(Data), .en(decoder_1_out11), .clk(Clock), .Q(register_11_q));  // open: clr
  Register #(.trigger("falling"), .width(32)) register_12 (
    .D(Data), .en(decoder_1_out12), .clk(Clock), .Q(register_12_q));  // open: clr
  Register #(.trigger("falling"), .width(32)) register_13 (
    .D(Data), .en(decoder_1_out13), .clk(Clock), .Q(register_13_q));  // open: clr
  Register #(.trigger("falling"), .width(32)) register_14 (
    .D(Data), .en(decoder_1_out14), .clk(Clock), .Q(register_14_q));  // open: clr
  Register #(.trigger("falling"), .width(32)) register_15 (
    .D(Data), .en(decoder_1_out15), .clk(Clock), .Q(register_15_q));  // open: clr

  // Notes on the sheet:
  //   ZERO
  //   RA
  //   SP
  //   GP
  //   TP
  //   T0
  //   T1
  //   T2
  //   S0
  //   S1
  //   A0
  //   A1
  //   S2
  //   S3
  //   S4
  //   S5
endmodule

module RegisterFile (
  input  [31:0] Data,
  input  [4:0] RD,
  input  Write,
  input  Clock,
  input  [4:0] RS1,
  input  [4:0] RS2,
  output [31:0] Out1,
  output [31:0] Out2
);

  wire demultiplexer_1_out0, demultiplexer_1_out1;
  wire [31:0] BottomRegisters_out1, BottomRegisters_out2, TopRegisters_out1, TopRegisters_out2;

  Demultiplexer demultiplexer_1 (.out0(demultiplexer_1_out0), .out1(demultiplexer_1_out1), .in(Write), .sel(RD[4]));
  Registers16WithZero BottomRegisters (
    .Write(demultiplexer_1_out0), .RD(RD[3:0]), .Clock(Clock), .Data(Data), .RS1(RS1[3:0]), .RS2(RS2[3:0]),
    .Out1(BottomRegisters_out1), .Out2(BottomRegisters_out2));
  Registers16 TopRegisters (
    .Write(demultiplexer_1_out1), .RD(RD[3:0]), .Clock(Clock), .Data(Data), .RS1(RS1[3:0]), .RS2(RS2[3:0]),
    .Out1(TopRegisters_out1), .Out2(TopRegisters_out2));
  Multiplexer #(.width(32)) multiplexer_1 (
    .in0(BottomRegisters_out1), .in1(TopRegisters_out1), .out(Out1), .sel(RS1[4]));
  Multiplexer #(.width(32)) multiplexer_2 (
    .in0(BottomRegisters_out2), .in1(TopRegisters_out2), .out(Out2), .sel(RS2[4]));
endmodule

module CPU (
  input  [31:0] Instruction,
  input  [31:0] LoadValue,
  input  Clock,
  input  Reset,
  output Illegal,
  output [2:0] MemWidth,
  output Store,
  output Load,
  output [31:0] MemAddr,
  output [31:0] StoreValue,
  output [31:0] PC
);

  wire and_1_out, and_2_out, branchunit_1_branch, d_ff_1_q, d_ff_2_q, decoder_1_out0, decoder_1_out3,
       decoder_1_out4, decoder_1_out5, decoder_1_out8, decoder_1_out12, decoder_1_out13, decoder_1_out24,
       decoder_1_out25, decoder_1_out27, ex_mem_wbregisters2_1_obufsignal, ex_mem_wbregisters2_2_obufsignal,
       ex_mem_wbregisters2_3_obufsignal, ex_mem_wbregisters2_4_obufsignal, ex_memregisters_1_owrite,
       ex_memregisters_1_rillegal, id_exregisters3_1_out0, id_exregisters3_1_out1, id_exregisters3_1_out2,
       id_exregisters3_1_out3, id_exregisters3_1_out4, id_exregisters3_1_out5, id_exregisters3_1_out6,
       id_exregisters4_1_out1, id_exregisters4_1_out2, id_exregisters4_1_out3, mem_wbregisters1_1_owrite,
       mem_wbregisters3_2_obufsignal, nand_1_out, not_1_out, or_1_out, or_2_out, or_3_out, or_4_out,
       or_5_out, or_6_out, or_7_out, or_8_out, or_9_out, priority_encoder_1_p1, priority_encoder_1_p2,
       priority_encoder_1_p3, priority_encoder_1_p4, priority_encoder_1_p6, priority_encoder_1_p7,
       priority_encoder_1_p8;
  wire [1:0] extractor_1_opcode, forwardingunit_ex_1_forward_rs1, forwardingunit_ex_1_forward_rs2;
  wire [2:0] extractor_1_funct3, id_exregisters1_1_out_fanct3, priority_encoder_1_p5;
  wire [4:0] ex_memregisters_1_ord, extractor_1_opcode_2, extractor_1_rd, extractor_1_rs1, extractor_1_rs2,
       id_exregisters1_1_out_rd, id_exregisters1_1_out_rs1, id_exregisters1_1_out_rs2, mem_wbregisters1_1_ord;
  wire [6:0] extractor_1_funct7, id_exregisters1_1_out_fanct7;
  wire [31:0] adder_1_out, adder_2_out, adder_3_out, adder_4_out, adder_5_out, alu_1_data,
       controlled_buffer_1_out, ex_mem_wbregisters2_1_odata, ex_mem_wbregisters2_2_odata,
       ex_mem_wbregisters2_3_odata, ex_mem_wbregisters2_4_odata, ex_mem_wbregisters2_4_odataex,
       extractor_1_immediate, id_exregisters1_1_out_immediate, id_exregisters2_1_rout1,
       id_exregisters2_1_rout2, if_idregisters_1_inst_id, mem_wbregisters3_2_odata, multiplexer_1_out,
       multiplexer_2_out, multiplexer_3_out, multiplexer_4_out, multiplexer_5_out, multiplexer_6_out,
       register_1_q, registerfile_1_out1, registerfile_1_out2;

  or or_1 (or_1_out, Reset, or_3_out);
  IF_IDregisters if_idregisters_1 (
    .Instruction(Instruction), .PC(register_1_q), .R(or_1_out), .WE(1'b1), .Clock(Clock),
    .Inst_ID(if_idregisters_1_inst_id), .PC_ID(PC));
  MEM_WBregisters3 mem_wbregisters3_1 (
    .bufsignal(ex_memregisters_1_rillegal), .WE(1'b1), .Clock(Clock), .R(or_1_out), .Obufsignal(Illegal));  // open: data, Odata
  D_Flip_Flop d_ff_1 (.D(1'b1), .clk(Clock), .Q(d_ff_1_q), .reset(or_1_out));  // open: Qn, preset
  D_Flip_Flop d_ff_2 (.D(d_ff_1_q), .clk(Clock), .Q(d_ff_2_q), .reset(or_1_out));  // open: Qn, preset
  and and_1 (and_1_out, d_ff_2_q, or_2_out);
  Extractor extractor_1 (
    .Instruction(if_idregisters_1_inst_id), .Format(priority_encoder_1_p5),
    .Opcode({extractor_1_opcode_2, extractor_1_opcode}), .RD(extractor_1_rd), .Funct3(extractor_1_funct3),
    .RS1(extractor_1_rs1), .RS2(extractor_1_rs2), .funct7(extractor_1_funct7),
    .Immediate(extractor_1_immediate));
  Register #(.trigger("falling"), .width(32)) register_1 (
    .D(multiplexer_1_out), .en(1'b1), .clk(Clock), .Q(register_1_q), .clr(or_1_out));
  ID_EXregisters1 id_exregisters1_1 (
    .RD(extractor_1_rd), .Fanct3(extractor_1_funct3), .RS1(extractor_1_rs1), .RS2(extractor_1_rs2),
    .fanct7(extractor_1_funct7), .Immediate(extractor_1_immediate), .WE(1'b1), .Clock(Clock), .R(or_1_out),
    .out_RD(id_exregisters1_1_out_rd), .out_Fanct3(id_exregisters1_1_out_fanct3),
    .out_RS1(id_exregisters1_1_out_rs1), .out_RS2(id_exregisters1_1_out_rs2),
    .out_fanct7(id_exregisters1_1_out_fanct7), .out_Immediate(id_exregisters1_1_out_immediate));
  Multiplexer #(.width(32)) multiplexer_1 (
    .in0(adder_3_out), .in1(multiplexer_2_out), .out(multiplexer_1_out), .sel(or_3_out));
  EX_MEM_WBregisters2 ex_mem_wbregisters2_1 (
    .data(adder_1_out), .bufsignal(id_exregisters3_1_out2), .WE(1'b1), .Clock(Clock), .R(or_1_out),
    .Odata(ex_mem_wbregisters2_1_odata), .Obufsignal(ex_mem_wbregisters2_1_obufsignal));  // open: OdataEX
  Decoder #(.select(5)) decoder_1 (
    .out0(decoder_1_out0), .out3(decoder_1_out3), .out4(decoder_1_out4), .out5(decoder_1_out5),
    .out8(decoder_1_out8), .out12(decoder_1_out12), .out13(decoder_1_out13), .out24(decoder_1_out24),
    .out25(decoder_1_out25), .out27(decoder_1_out27), .sel(extractor_1_opcode_2));  // open: out1, out2, out6, out7, out9, out10, out11, out14, out15, out16, out17, out18, out19, out20, out21, out22, out23, out26, out28, out29, out30, out31, en
  MEM_WBregisters1 mem_wbregisters1_1 (
    .RD(ex_memregisters_1_ord), .write(ex_memregisters_1_owrite), .WE(1'b1), .Clock(Clock), .R(or_1_out),
    .ORD(mem_wbregisters1_1_ord), .Owrite(mem_wbregisters1_1_owrite));
  Adder #(.width(32)) adder_1 (.a(PC), .b(id_exregisters1_1_out_immediate), .out(adder_1_out));  // open: cin, cout
  Multiplexer #(.width(32)) multiplexer_2 (
    .in0(adder_2_out), .in1(adder_4_out), .out(multiplexer_2_out), .sel(id_exregisters4_1_out3));
  or or_2 (or_2_out, nand_1_out, not_1_out);
  nand nand_1 (nand_1_out, extractor_1_opcode[1], extractor_1_opcode[0]);
  assign controlled_buffer_1_out = ex_mem_wbregisters2_1_obufsignal ? ex_mem_wbregisters2_1_odata : 32'bz;  // Controlled_Buffer controlled_buffer_1
  Adder #(.width(32)) adder_2 (.a(PC), .b(multiplexer_3_out), .out(adder_2_out));  // open: cin, cout
  assign controlled_buffer_1_out = ex_mem_wbregisters2_3_obufsignal ? ex_mem_wbregisters2_3_odata : 32'bz;  // Controlled_Buffer controlled_buffer_2
  Adder #(.width(32)) adder_3 (.a(PC), .b(32'h4), .out(adder_3_out));  // open: cin, cout
  or or_3 (or_3_out, id_exregisters4_1_out3, id_exregisters4_1_out2);
  not not_1 (not_1_out, priority_encoder_1_p7);
  Multiplexer #(.width(32)) multiplexer_3 (
    .in0(32'h4), .in1(id_exregisters1_1_out_immediate), .out(multiplexer_3_out), .sel(id_exregisters4_1_out2));
  RegisterFile registerfile_1 (
    .Data(controlled_buffer_1_out), .RD(mem_wbregisters1_1_ord), .Write(mem_wbregisters1_1_owrite),
    .Clock(Clock), .RS1(id_exregisters1_1_out_rs1), .RS2(id_exregisters1_1_out_rs2),
    .Out1(registerfile_1_out1), .Out2(registerfile_1_out2));
  ID_EXregisters4 id_exregisters4_1 (
    .in1(or_4_out), .in2(or_6_out), .in3(decoder_1_out25), .WE(1'b1), .Clock(Clock), .R(or_1_out),
    .out1(id_exregisters4_1_out1), .out2(id_exregisters4_1_out2), .out3(id_exregisters4_1_out3));
  ForwardingUnit_EX forwardingunit_ex_1 (
    .RS1_EX(id_exregisters1_1_out_rs1), .RD_MEM(ex_memregisters_1_ord), .RS2_EX(id_exregisters1_1_out_rs2),
    .RegWrite_MEM(ex_memregisters_1_owrite), .Forward_RS1(forwardingunit_ex_1_forward_rs1[0]),
    .Forward_RS2(forwardingunit_ex_1_forward_rs2[0]));
  ForwardingUnit_WB forwardingunit_wb_1 (
    .RS1_EX(id_exregisters1_1_out_rs1), .RD_WB(mem_wbregisters1_1_ord), .RS2_EX(id_exregisters1_1_out_rs2),
    .RegWrite_WB(mem_wbregisters1_1_owrite), .Forward_RS1(forwardingunit_ex_1_forward_rs1[1]),
    .Forward_RS2(forwardingunit_ex_1_forward_rs2[1]));
  ID_EXregisters2 id_exregisters2_1 (
    .Out1(registerfile_1_out1), .Out2(registerfile_1_out2), .WE(1'b1), .Clock(Clock), .R(or_1_out),
    .ROut1(id_exregisters2_1_rout1), .Rout2(id_exregisters2_1_rout2));
  EX_MEM_WBregisters2 ex_mem_wbregisters2_2 (
    .data(id_exregisters1_1_out_immediate), .bufsignal(id_exregisters3_1_out3), .WE(1'b1), .Clock(Clock),
    .R(or_1_out), .Odata(ex_mem_wbregisters2_2_odata), .Obufsignal(ex_mem_wbregisters2_2_obufsignal));  // open: OdataEX
  EX_MEM_WBregisters2 ex_mem_wbregisters2_3 (
    .data(adder_3_out), .bufsignal(id_exregisters4_1_out1), .WE(1'b1), .Clock(Clock), .R(or_1_out),
    .Odata(ex_mem_wbregisters2_3_odata), .Obufsignal(ex_mem_wbregisters2_3_obufsignal));  // open: OdataEX
  Multiplexer #(.select(2), .width(32)) multiplexer_4 (
    .in0(id_exregisters2_1_rout1), .in1(ex_mem_wbregisters2_4_odataex), .in2(ex_mem_wbregisters2_4_odata),
    .in3(ex_mem_wbregisters2_4_odataex), .out(multiplexer_4_out), .sel(forwardingunit_ex_1_forward_rs1));
  Multiplexer #(.select(2), .width(32)) multiplexer_5 (
    .in0(id_exregisters2_1_rout2), .in1(ex_mem_wbregisters2_4_odataex), .in2(ex_mem_wbregisters2_4_odata),
    .in3(ex_mem_wbregisters2_4_odataex), .out(multiplexer_5_out), .sel(forwardingunit_ex_1_forward_rs2));
  Multiplexer #(.width(32)) multiplexer_6 (
    .in0(multiplexer_5_out), .in1(id_exregisters1_1_out_immediate), .out(multiplexer_6_out),
    .sel(id_exregisters3_1_out6));
  or or_4 (or_4_out, decoder_1_out27, decoder_1_out25);
  or or_5 (or_5_out, decoder_1_out13, decoder_1_out5);
  // Priority_Encoder priority_encoder_1: pin names not known; wires that end beside it: priority_encoder_1_p1, priority_encoder_1_p2, priority_encoder_1_p3, priority_encoder_1_p4, priority_encoder_1_p5, priority_encoder_1_p6, priority_encoder_1_p7, priority_encoder_1_p8, 1'b0, 1'b0
  assign controlled_buffer_1_out = ex_mem_wbregisters2_2_obufsignal ? ex_mem_wbregisters2_2_odata : 32'bz;  // Controlled_Buffer controlled_buffer_3
  or or_6 (or_6_out, and_2_out, decoder_1_out27);
  or or_7 (or_7_out, decoder_1_out3, decoder_1_out4, decoder_1_out0, decoder_1_out25);
  Adder #(.width(32)) adder_4 (
    .a(multiplexer_4_out), .b(id_exregisters1_1_out_immediate), .out(adder_4_out));  // open: cin, cout
  and and_2 (and_2_out, branchunit_1_branch, decoder_1_out24);
  or or_8 (or_8_out, decoder_1_out25, decoder_1_out12, decoder_1_out4, decoder_1_out0, decoder_1_out5, decoder_1_out13, decoder_1_out27);
  or or_9 (or_9_out, decoder_1_out12, decoder_1_out4);
  BranchUnit branchunit_1 (
    .A(multiplexer_4_out), .B(multiplexer_6_out), .Funct3(id_exregisters1_1_out_fanct3),
    .Branch(branchunit_1_branch));
  ID_EXregisters3 id_exregisters3_1 (
    .in0(decoder_1_out8), .in1(decoder_1_out0), .in2(decoder_1_out5), .in3(decoder_1_out13), .in4(or_9_out),
    .in5(or_8_out), .in6(decoder_1_out4), .in7(or_7_out), .in8(decoder_1_out27), .in9(or_5_out),
    .in10(decoder_1_out24), .in11(decoder_1_out8), .in12(decoder_1_out12), .WE(1'b1), .Clock(Clock),
    .R(or_1_out), .out0(id_exregisters3_1_out0), .out1(id_exregisters3_1_out1),
    .out2(id_exregisters3_1_out2), .out3(id_exregisters3_1_out3), .out4(id_exregisters3_1_out4),
    .out5(id_exregisters3_1_out5), .out6(id_exregisters3_1_out6), .out7(priority_encoder_1_p2),
    .out8(priority_encoder_1_p8), .out9(priority_encoder_1_p6), .out10(priority_encoder_1_p4),
    .out11(priority_encoder_1_p3), .out12(priority_encoder_1_p1));
  EX_MEM_WBregisters2 ex_mem_wbregisters2_4 (
    .data(alu_1_data), .bufsignal(id_exregisters3_1_out4), .WE(1'b1), .Clock(Clock), .R(or_1_out),
    .Odata(ex_mem_wbregisters2_4_odata), .Obufsignal(ex_mem_wbregisters2_4_obufsignal),
    .OdataEX(ex_mem_wbregisters2_4_odataex));
  ALU alu_1 (
    .A(multiplexer_4_out), .B(multiplexer_6_out), .Funct3(id_exregisters1_1_out_fanct3),
    .funct7(id_exregisters1_1_out_fanct7), .Imm(id_exregisters3_1_out6), .Data(alu_1_data));
  assign controlled_buffer_1_out = ex_mem_wbregisters2_4_obufsignal ? ex_mem_wbregisters2_4_odata : 32'bz;  // Controlled_Buffer controlled_buffer_4
  assign controlled_buffer_1_out = mem_wbregisters3_2_obufsignal ? mem_wbregisters3_2_odata : 32'bz;  // Controlled_Buffer controlled_buffer_5
  Adder #(.width(32)) adder_5 (
    .a(multiplexer_4_out), .b(id_exregisters1_1_out_immediate), .out(adder_5_out));  // open: cin, cout
  MEM_WBregisters3 mem_wbregisters3_2 (
    .data(LoadValue), .bufsignal(Load), .WE(1'b1), .Clock(Clock), .R(or_1_out),
    .Odata(mem_wbregisters3_2_odata), .Obufsignal(mem_wbregisters3_2_obufsignal));
  EX_MEMregisters ex_memregisters_1 (
    .RD(id_exregisters1_1_out_rd), .write(id_exregisters3_1_out5), .Illegal(and_1_out),
    .MemWidth(id_exregisters1_1_out_fanct3), .Store(id_exregisters3_1_out0), .Load(id_exregisters3_1_out1),
    .MemAddr(adder_5_out), .StoreValue(multiplexer_6_out), .WE(1'b1), .Clock(Clock), .R(or_1_out),
    .ORD(ex_memregisters_1_ord), .Owrite(ex_memregisters_1_owrite), .RIllegal(ex_memregisters_1_rillegal),
    .RMemWidth(MemWidth), .RStore(Store), .RLoad(Load), .RMemAddr(MemAddr), .RStoreValue(StoreValue));

  // Notes on the sheet:
  //   AUIPC
  //   Store PC?
  //   Relative Jump?
  //   JALR
  //   A
  //   Imm
  //   B
endmodule

module ALU (
  input  [31:0] A,
  input  [31:0] B,
  input  [2:0] Funct3,
  input  [6:0] funct7,
  input  Imm,
  output [31:0] Data
);

  wire and_2_out, and_3_out, not_1_out;
  wire [0:0] comparator_1_lt, comparator_2_lt;
  wire [31:0] adder_1_out, and_1_out, divider_1_out, divider_1_rem, divider_2_out, divider_2_rem,
       multiplexer_1_out, multiplexer_2_out, multiplexer_3_out, multiplexer_4_out, multiplexer_6_out,
       negator_1_out, or_1_out, shifter_1_out, shifter_2_out, shifter_3_out, subtractor_1_out, xor_1_out;
  wire [63:0] multiplier_1_out, multiplier_2_out, multiplier_3_out, negator_2_out;

  not not_1 (not_1_out, Imm);
  assign xor_1_out = A ^ B;  // XOR_Gate xor_1, 32 bits wide
  assign or_1_out = A | B;  // OR_Gate or_1, 32 bits wide
  assign and_1_out = A & B;  // AND_Gate and_1, 32 bits wide
  Shifter #(.width(32)) shifter_1 (.in(A), .\dist (B[4:0]), .out(shifter_1_out));
  Shifter #(.shift("lr"), .width(32)) shifter_2 (.in(A), .\dist (B[4:0]), .out(shifter_2_out));
  Shifter #(.shift("ar"), .width(32)) shifter_3 (.in(A), .\dist (B[4:0]), .out(shifter_3_out));
  Negator #(.width(32)) negator_1 (.in(B), .out(negator_1_out));
  Adder #(.width(32)) adder_1 (.a(A), .b(B), .out(adder_1_out));  // open: cin, cout
  Subtractor #(.width(32)) subtractor_1 (.a(A), .b(B), .out(subtractor_1_out));  // open: bin, bout
  and and_2 (and_2_out, funct7[5], not_1_out);
  Comparator #(.width(32)) comparator_1 (.a(A), .b(B), .lt(comparator_1_lt[0]));  // open: gt, eq
  Comparator #(.mode("unsigned"), .width(32)) comparator_2 (.a(A), .b(B), .lt(comparator_2_lt[0]));  // open: gt, eq
  Multiplexer #(.width(32)) multiplexer_1 (
    .in0(shifter_2_out), .in1(shifter_3_out), .out(multiplexer_1_out), .sel(funct7[5]));
  Multiplexer #(.width(32)) multiplexer_2 (
    .in0(adder_1_out), .in1(subtractor_1_out), .out(multiplexer_2_out), .sel(and_2_out));
  Divider #(.width(32)) divider_1 (.a(A), .b(B), .out(divider_1_out), .rem(divider_1_rem));  // open: upper
  Divider #(.mode("twosComplement"), .width(32)) divider_2 (
    .a(A), .b(B), .out(divider_2_out), .rem(divider_2_rem));  // open: upper
  Multiplexer #(.select(3), .width(32)) multiplexer_3 (
    .in0(multiplier_3_out[31:0]), .in1(multiplier_3_out[63:32]), .in2(multiplexer_6_out),
    .in3(multiplier_2_out[63:32]), .in4(divider_2_out), .in5(divider_1_out), .in6(divider_2_rem),
    .in7(divider_1_rem), .out(multiplexer_3_out), .sel(Funct3));
  Multiplexer #(.select(3), .width(32)) multiplexer_4 (
    .in0(multiplexer_2_out), .in1(shifter_1_out), .in2({{31{1'b0}}, comparator_1_lt[0]}),
    .in3({{31{1'b0}}, comparator_2_lt[0]}), .in4(xor_1_out), .in5(multiplexer_1_out), .in6(or_1_out),
    .in7(and_1_out), .out(multiplexer_4_out), .sel(Funct3));
  Multiplier #(.width(64)) multiplier_1 (
    .a({{32{1'b0}}, negator_1_out}), .b({{32{1'b0}}, A}), .out(multiplier_1_out));  // open: cin, cout
  Multiplexer #(.width(32)) multiplexer_5 (
    .in0(multiplexer_4_out), .in1(multiplexer_3_out), .out(Data), .sel(and_3_out));
  and and_3 (and_3_out, funct7[0], ~Imm);  // AND_Gate
  Negator #(.width(64)) negator_2 (.in(multiplier_1_out), .out(negator_2_out));
  Multiplier #(.width(64)) multiplier_2 (
    .a({{32{1'b0}}, B}), .b({{32{1'b0}}, A}), .out(multiplier_2_out));  // open: cin, cout
  Multiplexer #(.width(32)) multiplexer_6 (
    .in0(negator_2_out[63:32]), .in1(multiplier_2_out[63:32]), .out(multiplexer_6_out),
    .sel(negator_1_out[31]));
  Multiplier #(.mode("twosComplement"), .width(64)) multiplier_3 (
    .a({{33{B[31]}}, B[30:0]}), .b({{33{A[31]}}, A[30:0]}), .out(multiplier_3_out));  // open: cin, cout
endmodule

module BranchUnit (
  input  [31:0] A,
  input  [31:0] B,
  input  [2:0] Funct3,
  output Branch
);

  wire comparator_1_eq, comparator_1_gt, comparator_1_lt, comparator_2_eq, comparator_2_gt, comparator_2_lt,
       not_1_out, or_1_out, or_2_out;

  Comparator #(.mode("unsigned"), .width(32)) comparator_1 (
    .a(A), .b(B), .gt(comparator_1_gt), .eq(comparator_1_eq), .lt(comparator_1_lt));
  Comparator #(.width(32)) comparator_2 (
    .a(A), .b(B), .gt(comparator_2_gt), .eq(comparator_2_eq), .lt(comparator_2_lt));
  not not_1 (not_1_out, comparator_1_eq);
  or or_1 (or_1_out, comparator_1_gt, comparator_1_eq);
  or or_2 (or_2_out, comparator_2_gt, comparator_2_eq);
  Multiplexer #(.select(3)) multiplexer_1 (
    .in0(comparator_1_eq), .in1(not_1_out), .in2(1'b0), .in3(1'b0), .in4(comparator_2_lt), .in5(or_2_out),
    .in6(comparator_1_lt), .in7(or_1_out), .out(Branch), .sel(Funct3));
endmodule

module Memory (
  input  [2:0] Width,
  input  Store,
  input  Load,
  input  [31:0] Address,
  input  [31:0] StoreValue,
  input  Clock,
  output [31:0] LoadValue
);

  wire not_1_out, not_2_out, not_3_out, not_4_out, or_1_out;
  wire [1:0] subtractor_1_out_2;
  wire [31:0] multiplexer_1_out, multiplexer_2_out, multiplexer_3_out, multiplexer_4_out, multiplexer_5_out,
       multiplexer_7_out, multiplexer_8_out, multiplexer_9_out, multiplexer_10_out, multiplexer_11_out,
       multiplexer_12_out, ram_1_dout, ram_1_dout_2;
  wire [31:2] subtractor_1_out;
  wire [31:8] ram_1_dout_3, ram_1_dout_4;

  Subtractor #(.width(32)) subtractor_1 (
    .a(Address), .b(32'h1000000), .out({subtractor_1_out, subtractor_1_out_2}));  // open: bin, bout
  or or_1 (or_1_out, Store, Load);
  Multiplexer #(.width(32)) multiplexer_1 (
    .in0({ram_1_dout_4[31], ram_1_dout_4[14:8], ram_1_dout_3[31], ram_1_dout_3[14:8], StoreValue[15:0]}),
    .in1({ram_1_dout_4[31], ram_1_dout_4[14:8], StoreValue[15:0], ram_1_dout[31], ram_1_dout[6:0]}),
    .out(multiplexer_1_out), .sel(subtractor_1_out_2[0]));
  Multiplexer #(.width(32)) multiplexer_2 (
    .in0(multiplexer_1_out),
    .in1({StoreValue[15:0], ram_1_dout_2[31], ram_1_dout_2[6:0], ram_1_dout[31], ram_1_dout[6:0]}),
    .out(multiplexer_2_out), .sel(subtractor_1_out_2[1]));
  Multiplexer #(.select(2), .width(32)) multiplexer_3 (
    .in0({ram_1_dout_4[31], ram_1_dout_4[14:8], ram_1_dout_3[31], ram_1_dout_3[14:8], ram_1_dout_2[31], ram_1_dout_2[6:0], StoreValue[7:0]}),
    .in1({ram_1_dout_4[31], ram_1_dout_4[14:8], ram_1_dout_3[31], ram_1_dout_3[14:8], StoreValue[7:0], ram_1_dout[31], ram_1_dout[6:0]}),
    .in2({ram_1_dout_4[31], ram_1_dout_4[14:8], StoreValue[7:0], ram_1_dout_2[31], ram_1_dout_2[6:0], ram_1_dout[31], ram_1_dout[6:0]}),
    .in3({StoreValue[7:0], ram_1_dout_3[31], ram_1_dout_3[14:8], ram_1_dout_2[31], ram_1_dout_2[6:0], ram_1_dout[31], ram_1_dout[6:0]}),
    .out(multiplexer_3_out), .sel(subtractor_1_out_2));
  Multiplexer #(.width(32)) multiplexer_4 (
    .in0(StoreValue), .in1(multiplexer_5_out), .out(multiplexer_4_out), .sel(not_1_out));
  not not_1 (not_1_out, Width[1]);
  not not_2 (not_2_out, Width[0]);
  Multiplexer #(.width(32)) multiplexer_5 (
    .in0(multiplexer_2_out), .in1(multiplexer_3_out), .out(multiplexer_5_out), .sel(not_2_out));
  RAM #(.addrWidth(24), .asyncread("true"), .dataWidth(32), .trigger("falling")) ram_1 (
    .addr(subtractor_1_out[25:2]), .we(Store), .oe(or_1_out), .clk(Clock), .din(multiplexer_4_out),
    .dout({ram_1_dout_4[31], ram_1_dout_4[14:8], ram_1_dout_3[31], ram_1_dout_3[14:8], ram_1_dout_2[31], ram_1_dout_2[6:0], ram_1_dout[31], ram_1_dout[6:0]}));
  Multiplexer #(.width(32)) multiplexer_6 (
    .in0({ram_1_dout_4[31], ram_1_dout_4[14:8], ram_1_dout_3[31], ram_1_dout_3[14:8], ram_1_dout_2[31], ram_1_dout_2[6:0], ram_1_dout[31], ram_1_dout[6:0]}),
    .in1(multiplexer_8_out), .out(LoadValue), .sel(not_3_out));
  not not_3 (not_3_out, Width[1]);
  not not_4 (not_4_out, Width[0]);
  Multiplexer #(.width(32)) multiplexer_7 (
    .in0({{17{ram_1_dout_2[31]}}, ram_1_dout_2[6:0], ram_1_dout[31], ram_1_dout[6:0]}),
    .in1({{17{ram_1_dout_3[31]}}, ram_1_dout_3[14:8], ram_1_dout_2[31], ram_1_dout_2[6:0]}),
    .out(multiplexer_7_out), .sel(subtractor_1_out_2[0]));
  Multiplexer #(.width(32)) multiplexer_8 (
    .in0(multiplexer_11_out), .in1(multiplexer_12_out), .out(multiplexer_8_out), .sel(not_4_out));
  Multiplexer #(.width(32)) multiplexer_9 (
    .in0(multiplexer_7_out),
    .in1({{17{ram_1_dout_4[31]}}, ram_1_dout_4[14:8], ram_1_dout_3[31], ram_1_dout_3[14:8]}),
    .out(multiplexer_9_out), .sel(subtractor_1_out_2[1]));
  Multiplexer #(.select(2), .width(32)) multiplexer_10 (
    .in0({{25{ram_1_dout[31]}}, ram_1_dout[6:0]}), .in1({{25{ram_1_dout_2[31]}}, ram_1_dout_2[6:0]}),
    .in2({{25{ram_1_dout_3[31]}}, ram_1_dout_3[14:8]}), .in3({{25{ram_1_dout_4[31]}}, ram_1_dout_4[14:8]}),
    .out(multiplexer_10_out), .sel(subtractor_1_out_2));
  Multiplexer #(.width(32)) multiplexer_11 (
    .in0(multiplexer_9_out), .in1({{16{1'b0}}, multiplexer_9_out[15:0]}), .out(multiplexer_11_out),
    .sel(Width[2]));
  Multiplexer #(.width(32)) multiplexer_12 (
    .in0(multiplexer_10_out), .in1({{24{1'b0}}, multiplexer_10_out[7:0]}), .out(multiplexer_12_out),
    .sel(Width[2]));
endmodule

module ID_EXregisters1 (
  input  [4:0] RD,
  input  [2:0] Fanct3,
  input  [4:0] RS1,
  input  [4:0] RS2,
  input  [6:0] fanct7,
  input  [31:0] Immediate,
  input  WE,
  input  Clock,
  input  R,
  output [4:0] out_RD,
  output [2:0] out_Fanct3,
  output [4:0] out_RS1,
  output [4:0] out_RS2,
  output [6:0] out_fanct7,
  output [31:0] out_Immediate
);

  Register #(.width(5)) register_1 (.D(RD), .en(WE), .clk(Clock), .Q(out_RD), .clr(R));
  Register #(.width(3)) register_2 (.D(Fanct3), .en(WE), .clk(Clock), .Q(out_Fanct3), .clr(R));
  Register #(.width(5)) register_3 (.D(RS1), .en(WE), .clk(Clock), .Q(out_RS1), .clr(R));
  Register #(.width(5)) register_4 (.D(RS2), .en(WE), .clk(Clock), .Q(out_RS2), .clr(R));
  Register #(.width(7)) register_5 (.D(fanct7), .en(WE), .clk(Clock), .Q(out_fanct7), .clr(R));
  Register #(.width(32)) register_6 (.D(Immediate), .en(WE), .clk(Clock), .Q(out_Immediate), .clr(R));
endmodule

module ID_EXregisters2 (
  input  [31:0] Out1,
  input  [31:0] Out2,
  input  WE,
  input  Clock,
  input  R,
  output [31:0] ROut1,
  output [31:0] Rout2
);

  Register #(.width(32)) register_1 (.D(Out1), .en(WE), .clk(Clock), .Q(ROut1), .clr(R));
  Register #(.width(32)) register_2 (.D(Out2), .en(WE), .clk(Clock), .Q(Rout2), .clr(R));
endmodule

module EX_MEMregisters (
  input  [4:0] RD,
  input  write,
  input  Illegal,
  input  [2:0] MemWidth,
  input  Store,
  input  Load,
  input  [31:0] MemAddr,
  input  [31:0] StoreValue,
  input  WE,
  input  Clock,
  input  R,
  output [4:0] ORD,
  output Owrite,
  output RIllegal,
  output [2:0] RMemWidth,
  output RStore,
  output RLoad,
  output [31:0] RMemAddr,
  output [31:0] RStoreValue
);

  Register #(.trigger("falling"), .width(5)) register_1 (.D(RD), .en(WE), .clk(Clock), .Q(ORD), .clr(R));
  Register #(.trigger("falling"), .width(1)) register_2 (.D(write), .en(WE), .clk(Clock), .Q(Owrite), .clr(R));
  Register #(.trigger("falling"), .width(1)) register_3 (.D(Illegal), .en(WE), .clk(Clock), .Q(RIllegal), .clr(R));
  Register #(.trigger("falling"), .width(3)) register_4 (.D(MemWidth), .en(WE), .clk(Clock), .Q(RMemWidth), .clr(R));
  Register #(.trigger("falling"), .width(1)) register_5 (.D(Store), .en(WE), .clk(Clock), .Q(RStore), .clr(R));
  Register #(.trigger("falling"), .width(1)) register_6 (.D(Load), .en(WE), .clk(Clock), .Q(RLoad), .clr(R));
  Register #(.trigger("falling"), .width(32)) register_7 (.D(MemAddr), .en(WE), .clk(Clock), .Q(RMemAddr), .clr(R));
  Register #(.trigger("falling"), .width(32)) register_8 (
    .D(StoreValue), .en(WE), .clk(Clock), .Q(RStoreValue), .clr(R));
endmodule

module IF_IDregisters (
  input  [31:0] Instruction,
  input  [31:0] PC,
  input  R,
  input  WE,
  input  Clock,
  output [31:0] Inst_ID,
  output [31:0] PC_ID
);

  Register #(.trigger("falling"), .width(32)) register_1 (.D(PC), .en(WE), .clk(Clock), .Q(PC_ID), .clr(R));
  Register #(.trigger("falling"), .width(32)) register_2 (.D(Instruction), .en(WE), .clk(Clock), .Q(Inst_ID), .clr(R));
endmodule

module ID_EXregisters3 (
  input  in0,
  input  in1,
  input  in2,
  input  in3,
  input  in4,
  input  in5,
  input  in6,
  input  in7,
  input  in8,
  input  in9,
  input  in10,
  input  in11,
  input  in12,
  input  WE,
  input  Clock,
  input  R,
  output out0,
  output out1,
  output out2,
  output out3,
  output out4,
  output out5,
  output out6,
  output out7,
  output out8,
  output out9,
  output out10,
  output out11,
  output out12
);

  Register #(.width(1)) register_1 (.D(in0), .en(WE), .clk(Clock), .Q(out0), .clr(R));
  Register #(.width(1)) register_2 (.D(in1), .en(WE), .clk(Clock), .Q(out1), .clr(R));
  Register #(.width(1)) register_3 (.D(in2), .en(WE), .clk(Clock), .Q(out2), .clr(R));
  Register #(.width(1)) register_4 (.D(in3), .en(WE), .clk(Clock), .Q(out3), .clr(R));
  Register #(.width(1)) register_5 (.D(in4), .en(WE), .clk(Clock), .Q(out4), .clr(R));
  Register #(.width(1)) register_6 (.D(in5), .en(WE), .clk(Clock), .Q(out5), .clr(R));
  Register #(.width(1)) register_7 (.D(in6), .en(WE), .clk(Clock), .Q(out6), .clr(R));
  Register #(.width(1)) register_8 (.D(in7), .en(WE), .clk(Clock), .Q(out7), .clr(R));
  Register #(.width(1)) register_9 (.D(in8), .en(WE), .clk(Clock), .Q(out8), .clr(R));
  Register #(.width(1)) register_10 (.D(in9), .en(WE), .clk(Clock), .Q(out9), .clr(R));
  Register #(.width(1)) register_11 (.D(in10), .en(WE), .clk(Clock), .Q(out10), .clr(R));
  Register #(.width(1)) register_12 (.D(in11), .en(WE), .clk(Clock), .Q(out11), .clr(R));
  Register #(.width(1)) register_13 (.D(in12), .en(WE), .clk(Clock), .Q(out12), .clr(R));
endmodule

module MEM_WBregisters1 (
  input  [4:0] RD,
  input  write,
  input  WE,
  input  Clock,
  input  R,
  output [4:0] ORD,
  output Owrite
);

  Register #(.trigger("falling"), .width(5)) register_1 (.D(RD), .en(WE), .clk(Clock), .Q(ORD), .clr(R));
  Register #(.trigger("falling"), .width(1)) register_2 (.D(write), .en(WE), .clk(Clock), .Q(Owrite), .clr(R));
endmodule

module EX_MEM_WBregisters2 (
  input  [31:0] data,
  input  bufsignal,
  input  WE,
  input  Clock,
  input  R,
  output [31:0] Odata,
  output Obufsignal,
  output [31:0] OdataEX
);

  wire register_2_q;

  Register #(.trigger("falling"), .width(32)) register_1 (.D(data), .en(WE), .clk(Clock), .Q(OdataEX), .clr(R));
  Register #(.trigger("falling"), .width(1)) register_2 (
    .D(bufsignal), .en(WE), .clk(Clock), .Q(register_2_q), .clr(R));
  Register #(.trigger("falling"), .width(32)) register_3 (.D(OdataEX), .en(WE), .clk(Clock), .Q(Odata), .clr(R));
  Register #(.trigger("falling"), .width(1)) register_4 (
    .D(register_2_q), .en(WE), .clk(Clock), .Q(Obufsignal), .clr(R));
endmodule

module ID_EXregisters4 (
  input  in1,
  input  in2,
  input  in3,
  input  WE,
  input  Clock,
  input  R,
  output out1,
  output out2,
  output out3
);

  Register #(.width(1)) register_1 (.D(in1), .en(WE), .clk(Clock), .Q(out1), .clr(R));
  Register #(.width(1)) register_2 (.D(in2), .en(WE), .clk(Clock), .Q(out2), .clr(R));
  Register #(.width(1)) register_3 (.D(in3), .en(WE), .clk(Clock), .Q(out3), .clr(R));
endmodule

module MEM_WBregisters3 (
  input  [31:0] data,
  input  bufsignal,
  input  WE,
  input  Clock,
  input  R,
  output [31:0] Odata,
  output Obufsignal
);

  Register #(.trigger("falling"), .width(32)) register_1 (.D(data), .en(WE), .clk(Clock), .Q(Odata), .clr(R));
  Register #(.trigger("falling"), .width(1)) register_2 (.D(bufsignal), .en(WE), .clk(Clock), .Q(Obufsignal), .clr(R));
endmodule

module ForwardingUnit_EX (
  input  [4:0] RS1_EX,
  input  [4:0] RD_MEM,
  input  [4:0] RS2_EX,
  input  RegWrite_MEM,
  output Forward_RS1,
  output Forward_RS2
);

  wire comparator_1_eq, comparator_2_eq, comparator_3_eq, not_1_out;

  Comparator #(.mode("unsigned"), .width(5)) comparator_1 (
    .a(RS1_EX), .b(RD_MEM), .eq(comparator_1_eq));  // open: gt, lt
  not not_1 (not_1_out, comparator_2_eq);
  Comparator #(.mode("unsigned"), .width(5)) comparator_2 (
    .a(RD_MEM), .b({5{1'b0}}), .eq(comparator_2_eq));  // open: gt, lt
  Comparator #(.mode("unsigned"), .width(5)) comparator_3 (
    .a(RS2_EX), .b(RD_MEM), .eq(comparator_3_eq));  // open: gt, lt
  and and_1 (Forward_RS1, comparator_1_eq, not_1_out, RegWrite_MEM);
  and and_2 (Forward_RS2, comparator_3_eq, not_1_out, RegWrite_MEM);
endmodule

module ForwardingUnit_WB (
  input  [4:0] RS1_EX,
  input  [4:0] RD_WB,
  input  [4:0] RS2_EX,
  input  RegWrite_WB,
  output Forward_RS1,
  output Forward_RS2
);

  wire comparator_1_eq, comparator_2_eq, comparator_3_eq, not_1_out;

  Comparator #(.mode("unsigned"), .width(5)) comparator_1 (
    .a(RS1_EX), .b(RD_WB), .eq(comparator_1_eq));  // open: gt, lt
  Comparator #(.mode("unsigned"), .width(5)) comparator_2 (
    .a(RD_WB), .b({5{1'b0}}), .eq(comparator_2_eq));  // open: gt, lt
  Comparator #(.mode("unsigned"), .width(5)) comparator_3 (
    .a(RS2_EX), .b(RD_WB), .eq(comparator_3_eq));  // open: gt, lt
  not not_1 (not_1_out, comparator_2_eq);
  and and_1 (Forward_RS1, comparator_1_eq, not_1_out, RegWrite_WB);
  and and_2 (Forward_RS2, comparator_3_eq, not_1_out, RegWrite_WB);
endmodule
